# Fritzing sketch taco_ldr (saved by Fritzing 1.0.0rc)
breadboards: 2

parts:
  Mod1 = Heltec WiFi LoRa 32 V2 [part_number=HTIT-WB32LA]
  IC1 = Voltage Regulator [package=78xxl]
  VCC1 = Battery block 9V
  M1 = fc-51 [package=THT]
  U1 = SN74LS14N [package="DIP14 [THT]"]
  C1 = Electrolytic Capacitor [capacitance=10µF voltage=16V package="100 mil [THT, electrolytic]"]
  C2 = Electrolytic Capacitor [capacitance=10µF voltage=16V package="100 mil [THT, electrolytic]"]
  Grove1 = Grove OLED 128x96  # not connected
  R1 = Resistor [tolerance=±5% resistance=10k package="0402 [SMD]"]
  R2 = Resistor [tolerance=±5% resistance=10k package="0402 [SMD]"]

nets:
  N1: Mod1.pin_6, R1.Pin_0, R2.Pin_1
  N2: Mod1.pin_7, U1.6Y
  N3: Mod1.pin_16, Mod1.pin_17, M1.pin3
  GND: Mod1.pin_20, IC1.GND, IC1.IN, IC1.OUT, VCC1.-, VCC1.+, M1.pin2, U1.GND, C1.-, C1.+, C2.-, C2.+, R1.Pin_1
  N4: Mod1.pin_21, Mod1.pin_22
  N5: M1.pin1, U1.6A

notes:
  Para o Throttle do Autopiloto ou Receptor de rádio RX
  Hélice Bipá a 5 mm de distância
